# Fritzing sketch rpi3_switch (saved by Fritzing 0.9.3b)
breadboards: 1

parts:
  Raspberry_Pi_1 = Raspberry Pi 3 [part_number=RPI-3-V1.2]
  R1 = Resistor [tolerance=±5% resistance=220 package=THT]
  S1 = Pushbutton [package="[THT]"]
  LED1 = LED - 5mm [color="Red (633nm)" package="5 mm [THT]"]
  R2 = Resistor [tolerance=±5% resistance=220 package=THT]

nets:
  N1: Raspberry_Pi_1.GPIO19, R2.Pin_1
  N2: Raspberry_Pi_1.GPIO26, R1.Pin_0
  N3: Raspberry_Pi_1.GND, S1.Pin_1, S1.Pin_2, LED1.cathode
  N4: R1.Pin_1, S1.Pin_3, S1.Pin_4
  N5: LED1.anode, R2.Pin_0
